# Fritzing sketch Spooler Controller (saved by Fritzing 0.9.6b)
breadboards: 1

parts:
  Part1 = Arduino Uno (Rev3)
  R1 = Rotary Potentiometer (Small) [maximum_resistance=100kΩ package=THT]
  R2 = Rotary Potentiometer (Small) [maximum_resistance=100kΩ package=THT]
  S1 = Pushbutton [package="[THT]"]
  S2 = Pushbutton [package="[THT]"]
  LCD1 = LCD screen
  S4 = Pushbutton [package="[THT]"]
  S5 = Pushbutton [package="[THT]"]
  Part2 = Adafruit I2C+SPI LCD Backpack [part_number="Adafruit #292"]
  U1 = RJ45 Jack [package=rj45-8]

nets:
  A0: Part1.A0, R1.wiper
  A1: Part1.A1, R2.wiper
  SDA: Part1.A4/SDA, Part2.DATA, U1.2
  SCL: Part1.A5/SCL, Part2.CLOCK, U1.3
  N1: Part1.D2, S4.Pin_1, S4.Pin_2
  N2: Part1.D3_PWM, S2.Pin_1, S2.Pin_2
  N3: Part1.D4, S1.Pin_1, S1.Pin_2
  N4: Part1.D5_PWM, S5.Pin_1, S5.Pin_2
  5V: Part1.5V, R1.leg1, R2.leg2, LCD1.VDD, LCD1.LED+, Part2.VCC
  GND: Part1.GND, R1.leg2, R2.leg1, S1.Pin_3, S1.Pin_4, S2.Pin_3, S2.Pin_4, LCD1.VSS, LCD1.R/W, S4.Pin_3, S4.Pin_4, S5.Pin_3, S5.Pin_4, Part2.GND, U1.4
  12V: Part1.VIN, U1.8
  N5: LCD1.V0, Part2.CONTRAST
  N6: LCD1.RS, Part2.RS
  N7: LCD1.E, Part2.E
  N8: LCD1.DB0, Part2.DB0
  N9: LCD1.DB1, Part2.DB1
  N10: LCD1.DB2, Part2.DB2
  N11: LCD1.DB3, Part2.DB3
  N12: LCD1.DB4, Part2.DB4
  N13: LCD1.DB5, Part2.DB5
  N14: LCD1.DB6, Part2.DB6
  N15: LCD1.DB7, Part2.DB7
  N16: LCD1.LED-, Part2.LEDK

custom parts:
  Adafruit I2C+SPI LCD Backpack: LCD backpacks reduce the number of pins needed to connect to an LCD. LCDs are a fun and easy way to have your microcontroller project talk back to you. Character LCDs are common, and easy to get, available in tons of colors and sizes. We've written tutorials on using character LCDs with an Arduino (or similar microcontroller) but find that the number of pins necessary to control the LCD can be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
