# Fritzing sketch Spooler Motor Adaptor (saved by Fritzing 0.9.8b)
breadboards: 1

parts:
  JACK1 = 2.1mm DC Barrel Jack
  M1 = DC Motor
  D1 = Rectifier Diode [part_number=1N4001 package="300 mil [THT]"]

nets:
  N1: JACK1.center, M1.pin_1, D1.cathode
  N2: JACK1.sleeve, M1.pin_2, D1.anode

custom parts:
  2.1mm DC Barrel Jack: 2.1mm DC Barrel Jack with Thru-Hole Connectors (breadboardable)
