# Fritzing sketch Spooler, Fan Driver (saved by Fritzing 0.9.7b)
perfboards: 1

parts:
  Q1 = Basic FET N-Channel [part_number=NTE2984 package="TO220 [THT]"]
  D1 = Rectifier Diode [part_number=1N4001 package="300 mil [THT]"]
  D2 = Rectifier Diode [part_number=1N4001 package="300 mil [THT]"]
  J2 = Screw terminal - 2 pins [package=THT]
  J3 = Screw terminal - 2 pins [package=THT]  # not connected
  J5 = Screw terminal - 2 pins [package=THT]  # not connected
  R1 = Resistor [tolerance=±5% power=0.25 resistance=10k package=THT]
  J6 = Screw terminal - 2 pins [package=THT]
  J7 = Screw terminal - 2 pins [package=THT]
  Q2 = Basic FET N-Channel [package="TO220 [THT]"]
  D3 = Rectifier Diode [part_number=1N4001 package="300 mil [THT]"]
  D4 = Rectifier Diode [part_number=1N4001 package="300 mil [THT]"]
  J9 = Screw terminal - 2 pins [package=THT]
  R3 = Resistor [tolerance=±5% power=0.25 resistance=150 package=THT]
  R4 = Resistor [tolerance=±5% power=0.25 resistance=150 package=THT]
  R5 = Resistor [tolerance=±5% power=0.25 resistance=10k package=THT]

nets:
  N1: Q1.gate, R3.Pin_0
  N2: Q1.drain, D2.cathode
  N3: Q1.source, R1.Pin_1
  N4: D1.cathode, J2.pin2
  N5: D1.anode, D2.anode
  N6: R1.Pin_0, R3.Pin_1
  MOTOR: J6.pin1, D3.anode, D4.anode
  12V: J6.pin2, J7.pin1, D3.cathode
  GND: J7.pin2, Q2.source, J9.pin1, R5.Pin_0
  N7: Q2.gate, R4.Pin_0
  N8: Q2.drain, D4.cathode
  Signal: J9.pin2, R4.Pin_1, R5.Pin_1

notes:
  Left Terminals:
  Top: 5V, Gnd
  Mid: 5V Motor
  Low: Signal, Gnd
  Right Terminals:
  Top: 12V, Gnd
  Mid: 12V Motor
  Low: Signal, Gnd
  12V Power
  12V Motor
  5V Arduino
